# Fritzing sketch BeanDuino (saved by Fritzing 0.6.5b)
breadboards: 1

parts:
  Arduino1 = Arduino
  LCD1 = LCD screen
  R1 = Resistor [tolerance=±5% resistance=1k package=THT]
  R2 = Trimmer Potentiometer [maximum_resistance=10kΩ package=THT]
  IC1 = DIP - 8 pins [package="DIP (Dual Inline) [THT]"]
  J1 = Peltier Element
  Part1 = Bluetooth Mate Silver
  C2 = Tantalum Capacitor [capacitance="1 μF" package="100 mil [THT, tantalum]"]
  R8 = Resistor [tolerance=±5% resistance=200 package=THT]
  R6 = Resistor [tolerance=±5% resistance=200 package=THT]
  R7 = Resistor [tolerance=±5% resistance=200 package=THT]
  U1 = mystery part, 2 pins [chip_label=ssr spacing=300mil]
  S1 = Round Pushbutton
  S2 = Round Pushbutton
  S3 = Round Pushbutton
  S4 = Round Pushbutton

nets:
  N1: Arduino1.D13, LCD1.DB6
  N2: Arduino1.D12, LCD1.DB5
  N3: Arduino1.D11, LCD1.DB4
  N4: Arduino1.D10, LCD1.DB3
  N5: Arduino1.D9, LCD1.R/W
  N6: Arduino1.D8, LCD1.V0
  N7: Arduino1.D5, U1.pin2
  N8: Arduino1.D4, R8.Pin_0
  N9: Arduino1.D3, R6.Pin_0
  N10: Arduino1.D2, R7.Pin_0
  N11: Arduino1.D1TX, Part1.TX_5V
  N12: Arduino1.D0RX, Part1.RX_5V
  +5V: Arduino1.+5V, R1.Pin_0, R2.leg1, R2.leg2, IC1.Vdd, Part1.VCC, C2.+, S1.leg0, S2.leg0, S3.leg0, S4.leg0
  VSS: Arduino1.GND, LCD1.VSS, LCD1.RS, LCD1.LED+, IC1.Vss, IC1.T-, J1.pin2, Part1.CTS_5V, C2.-, U1.pin1
  N13: Arduino1.A0, S4.leg1
  N14: Arduino1.A1, S3.leg1
  N15: Arduino1.A2, S2.leg1
  N16: Arduino1.A3, S1.leg1
  N17: LCD1.VDD, R2.wiper
  N18: LCD1.DB7, R1.Pin_1
  N19: IC1.T+, J1.pin1
  N20: IC1.clock, R8.Pin_1
  N21: IC1.cs\, R6.Pin_1
  N22: IC1.data, R7.Pin_1

custom parts:
  DIP - 8 pins: A DIP stand-in part for whatever IC you want. With 8 pins on a 300 mil dual inline package (DIP) footprint.
